// Logisim project ALU_Unit.circ as structural Verilog: 3 circuits, main circuit main
module main (
  input  [3:0] A,
  input  [3:0] B,
  input  [1:0] S1_S0,
  input  [1:0] S3_S2,
  output [3:0] out_5
);

  wire [3:0] arithmetic_1_out_5, logic_1_e;

  Arithmetic arithmetic_1 (.A(A), .B(B), .in_3(S1_S0), .out_5(arithmetic_1_out_5));  // open: in_4, out_6
  Logic logic_1 (.A(A), .B(B), .in_3(S1_S0), .E(logic_1_e));
  Multiplexer #(.select(2), .width(4)) multiplexer_1 (
    .in0(arithmetic_1_out_5), .in1(logic_1_e), .in2({1'b0, A[3:1]}), .in3({A[2:0], 1'b0}), .out(out_5),
    .sel(S3_S2));  // open: en

  // Notes on the sheet:
  //   ALU Unit
endmodule

module Arithmetic (
  input  [3:0] A,
  input  [3:0] B,
  input  [1:0] in_3,
  input  in_4,
  output [3:0] out_5,
  output out_6
);

  wire adder_1_cout, adder_2_cout, adder_3_cout, multiplexer_1_out, multiplexer_2_out, multiplexer_3_out,
       multiplexer_4_out, not_1_out, not_2_out, not_3_out, not_4_out, not_5_out;

  not not_1 (not_1_out, 1'b1);
  not not_2 (not_2_out, B[0]);
  not not_3 (not_3_out, B[1]);
  not not_4 (not_4_out, B[2]);
  not not_5 (not_5_out, B[3]);
  Multiplexer #(.select(2)) multiplexer_1 (
    .in0(B[0]), .in1(not_2_out), .in2(not_1_out), .in3(1'b1), .out(multiplexer_1_out), .sel(in_3));  // open: en
  Multiplexer #(.select(2)) multiplexer_2 (
    .in0(B[1]), .in1(not_3_out), .in2(not_1_out), .in3(1'b1), .out(multiplexer_2_out), .sel(in_3));  // open: en
  Multiplexer #(.select(2)) multiplexer_3 (
    .in0(B[2]), .in1(not_4_out), .in2(not_1_out), .in3(1'b1), .out(multiplexer_3_out), .sel(in_3));  // open: en
  Multiplexer #(.select(2)) multiplexer_4 (
    .in0(B[3]), .in1(not_5_out), .in2(not_1_out), .in3(1'b1), .out(multiplexer_4_out), .sel(in_3));  // open: en
  Adder #(.width(1)) adder_1 (.a(A[0]), .b(multiplexer_1_out), .out(out_5[0]), .cin(in_4), .cout(adder_1_cout));
  Adder #(.width(1)) adder_2 (.a(A[1]), .b(multiplexer_2_out), .out(out_5[1]), .cin(adder_1_cout), .cout(adder_2_cout));
  Adder #(.width(1)) adder_3 (.a(A[2]), .b(multiplexer_3_out), .out(out_5[2]), .cin(adder_2_cout), .cout(adder_3_cout));
  Adder #(.width(1)) adder_4 (.a(A[3]), .b(multiplexer_4_out), .out(out_5[3]), .cin(adder_3_cout), .cout(out_6));

  // Other names for the same wires on the sheet: D0 = out_5[0]; D1 = out_5[1]; D2 = out_5[2]; D3 = out_5[3]

  // Notes on the sheet:
  //   Arithmetic Unit
endmodule

module Logic (
  input  [3:0] A,
  input  [3:0] B,
  input  [1:0] in_3,
  output [3:0] E
);

  wire [3:0] and_1_out, not_1_out, or_1_out, xor_1_out;

  assign and_1_out = A & B;  // AND_Gate and_1, 4 bits wide
  assign or_1_out = A | B;  // OR_Gate or_1, 4 bits wide
  assign xor_1_out = A ^ B;  // XOR_Gate xor_1, 4 bits wide
  assign not_1_out = ~A;  // NOT_Gate not_1, 4 bits wide
  Multiplexer #(.select(2), .width(4)) multiplexer_1 (
    .in0(and_1_out), .in1(or_1_out), .in2(xor_1_out), .in3(not_1_out), .out(E), .sel(in_3));  // open: en

  // Notes on the sheet:
  //   Logic Unit
endmodule
