// Logisim project Associative_Memory.circ as structural Verilog: 2 circuits, main circuit main
module main (
  input  [7:0] Word1,
  input  [7:0] Word2,
  input  [7:0] Argument,
  input  [7:0] Key,
  output Match1,
  output Match2
);

  wire not_1_out, not_2_out, not_3_out, not_4_out, not_5_out, not_6_out, not_7_out, not_8_out, or_1_out,
       or_2_out, or_3_out, or_4_out, or_5_out, or_6_out, or_7_out, or_8_out, or_9_out, or_10_out, or_11_out,
       or_12_out, or_13_out, or_14_out, or_15_out, or_16_out, xnor_1_out, xnor_2_out, xnor_3_out, xnor_4_out,
       xnor_5_out, xnor_6_out, xnor_7_out, xnor_8_out, xnor_9_out, xnor_10_out, xnor_11_out, xnor_12_out,
       xnor_13_out, xnor_14_out, xnor_15_out, xnor_16_out;

  not not_1 (not_1_out, Key[0]);
  not not_2 (not_2_out, Key[1]);
  not not_3 (not_3_out, Key[2]);
  not not_4 (not_4_out, Key[3]);
  not not_5 (not_5_out, Key[4]);
  not not_6 (not_6_out, Key[5]);
  not not_7 (not_7_out, Key[6]);
  not not_8 (not_8_out, Key[7]);
  xnor xnor_1 (xnor_1_out, Argument[0], Word1[0]);
  xnor xnor_2 (xnor_2_out, Argument[1], Word1[1]);
  xnor xnor_3 (xnor_3_out, Argument[2], Word1[2]);
  xnor xnor_4 (xnor_4_out, Argument[3], Word1[3]);
  xnor xnor_5 (xnor_5_out, Argument[4], Word1[4]);
  xnor xnor_6 (xnor_6_out, Argument[5], Word1[5]);
  xnor xnor_7 (xnor_7_out, Argument[6], Word1[6]);
  xnor xnor_8 (xnor_8_out, Argument[7], Word1[7]);
  xnor xnor_9 (xnor_9_out, Argument[0], Word2[0]);
  xnor xnor_10 (xnor_10_out, Argument[1], Word2[1]);
  xnor xnor_11 (xnor_11_out, Argument[2], Word2[2]);
  xnor xnor_12 (xnor_12_out, Argument[3], Word2[3]);
  xnor xnor_13 (xnor_13_out, Argument[4], Word2[4]);
  xnor xnor_14 (xnor_14_out, Argument[5], Word2[5]);
  xnor xnor_15 (xnor_15_out, Argument[6], Word2[6]);
  xnor xnor_16 (xnor_16_out, Argument[7], Word2[7]);
  or or_1 (or_1_out, xnor_1_out, not_1_out);
  or or_2 (or_2_out, xnor_2_out, not_2_out);
  or or_3 (or_3_out, xnor_3_out, not_3_out);
  or or_4 (or_4_out, xnor_4_out, not_4_out);
  or or_5 (or_5_out, xnor_5_out, not_5_out);
  or or_6 (or_6_out, xnor_6_out, not_6_out);
  or or_7 (or_7_out, xnor_7_out, not_7_out);
  or or_8 (or_8_out, xnor_8_out, not_8_out);
  or or_9 (or_9_out, xnor_9_out, not_1_out);
  or or_10 (or_10_out, xnor_10_out, not_2_out);
  or or_11 (or_11_out, xnor_11_out, not_3_out);
  or or_12 (or_12_out, xnor_12_out, not_4_out);
  or or_13 (or_13_out, xnor_13_out, not_5_out);
  or or_14 (or_14_out, xnor_14_out, not_6_out);
  or or_15 (or_15_out, xnor_15_out, not_7_out);
  or or_16 (or_16_out, xnor_16_out, not_8_out);
  and and_1 (Match1, or_1_out, or_2_out, or_3_out, or_4_out, or_5_out, or_6_out, or_7_out, or_8_out);
  and and_2 (Match2, or_9_out, or_10_out, or_11_out, or_12_out, or_13_out, or_14_out, or_15_out, or_16_out);

  // Other names for the same wires on the sheet: A0 = Argument[0]; A1 = Argument[1]; A2 = Argument[2];
  //   A3 = Argument[3]; A4 = Argument[4]; A5 = Argument[5]; A6 = Argument[6]; A7 = Argument[7]; K0 = Key[0];
  //   K1 = Key[1]; K2 = Key[2]; K3 = Key[3]; K4 = Key[4]; K5 = Key[5]; K6 = Key[6]; K7 = Key[7]; W00 = Word1[0];
  //   W01 = Word1[1]; W02 = Word1[2]; W03 = Word1[3]; W04 = Word1[4]; W05 = Word1[5]; W06 = Word1[6]; W07 = Word1[7];
  //   W10 = Word2[0]; W11 = Word2[1]; W12 = Word2[2]; W13 = Word2[3]; W14 = Word2[4]; W15 = Word2[5]; W16 = Word2[6];
  //   W17 = Word2[7]
endmodule

module Match (
  input  in_1,
  input  Wij
);
endmodule
