// Logisim project Control_Memory.circ as structural Verilog: 5 circuits, main circuit Control Unit
module Control_Unit (
  input  S,
  input  Z
);

  wire button_1_out, Decoding_Unit_i, multiplexer_1_out, SBR_Load;
  wire [1:0] BR, CAR_Logic_car_mux, CD;
  wire [5:2] MAP;
  wire [6:0] AD, CAR___1_car___1, CAR_q, multiplexer_2_out, SBR_q;
  wire [8:0] rom_1_data;

  Button button_1 (.out(button_1_out));
  Register #(.width(7)) SBR (.D(CAR___1_car___1), .en(SBR_Load), .Q(SBR_q), .clk(button_1_out));  // open: clr
  Multiplexer #(.select(2)) multiplexer_1 (
    .in0(1'b1), .in1(Decoding_Unit_i), .in2(S), .in3(Z), .out(multiplexer_1_out), .sel(CD));  // open: en
  CAR_Logic CAR_Logic (.BR(BR), .CD_Logic(multiplexer_1_out), .CAR_MUX(CAR_Logic_car_mux), .SBR_Load(SBR_Load));
  Incrementor CAR___1 (.CAR(CAR_q), .CAR___1(CAR___1_car___1));
  Multiplexer #(.select(2), .width(7)) multiplexer_2 (
    .in0(CAR___1_car___1), .in1(AD), .in2(SBR_q), .in3({1'b0, MAP, 2'b00}), .out(multiplexer_2_out),
    .sel(CAR_Logic_car_mux));  // open: en
  Register #(.width(7)) CAR (.D(multiplexer_2_out), .en(1'b1), .Q(CAR_q), .clk(button_1_out));  // open: clr
  ROM #(.addrWidth(7), .dataWidth(20)) rom_1 (.addr(CAR_q), .data({rom_1_data, CD, BR, AD}));  // open: sel
  Decoding_Unit Decoding_Unit (.MicroOPs(rom_1_data), .I(Decoding_Unit_i), .OPCODE(MAP), .CLOCK(button_1_out));

  // Notes on the sheet:
  //   contents of rom_1 (hex, n*v repeats v):
  //   283 10002 20005 10004 a0100 c0006 12807 a0180
endmodule

module Decoding_Unit (
  input  [8:0] MicroOPs,
  input  CLOCK,
  output [3:0] OPCODE,
  output I
);

  wire ADD, AR_LOAD, decoder_1_out7, DRTAR, INCPC, PCTAR, READ;
  wire [1:0] priority_encoder_1_out;
  wire [10:0] Address_Part_of_Instruction, Address_Register_q, multiplexer_1_out, PC;
  wire [15:0] AC, ALU_ac_load, Memory_Out, multiplexer_2_out;

  Decoder #(.select(3), .enable("false")) decoder_1 (
    .out1(ADD), .out5(DRTAR), .out6(PCTAR), .out7(decoder_1_out7), .sel(MicroOPs[8:6]));  // open: out0, out2, out3, out4
  or or_1 (AR_LOAD, DRTAR, PCTAR);
  Decoder #(.select(3), .enable("false")) decoder_2 (
    .out4(READ), .sel(MicroOPs[5:3]));  // open: out0, out1, out2, out3, out5, out6, out7
  Priority_Encoder #(.select(2), .disabled(0)) priority_encoder_1 (
    .in1(READ), .out(priority_encoder_1_out));  // open: in0, in2, in3, gs, en_out, en_in
  Multiplexer #(.width(11), .enable("false")) multiplexer_1 (
    .in0(Address_Part_of_Instruction), .in1(PC), .out(multiplexer_1_out), .sel(PCTAR));
  Multiplexer #(.select(2), .width(16), .enable("false")) multiplexer_2 (
    .in0({{5{1'b0}}, PC}), .in1(Memory_Out), .in2(AC), .out(multiplexer_2_out), .sel(priority_encoder_1_out));  // open: in3
  Decoder #(.select(3), .enable("false")) decoder_3 (
    .out5(INCPC), .sel(MicroOPs[2:0]));  // open: out0, out1, out2, out3, out4, out6, out7
  ALU ALU (.AC(AC), .DR({I, OPCODE, Address_Part_of_Instruction}), .AC_Load(ALU_ac_load));
  RAM #(.addrWidth(11), .dataWidth(16), .bus("separate")) ram_1 (
    .addr(Address_Register_q), .din({I, OPCODE, Address_Part_of_Instruction}), .data(Memory_Out),
    .str(decoder_1_out7), .clk(CLOCK), .ld(READ));  // open: sel, clr
  Register #(.width(11)) Address_Register (
    .D(multiplexer_1_out), .en(AR_LOAD), .Q(Address_Register_q), .clk(CLOCK));  // open: clr
  Counter #(.width(11), .max('h7ff)) Program_Counter (.count(INCPC), .Q(PC), .clk(CLOCK));  // open: load, D, carry, clr
  Register #(.width(16)) Data_Register (
    .D(multiplexer_2_out), .en(READ), .Q({I, OPCODE, Address_Part_of_Instruction}), .clk(CLOCK));  // open: clr
  Register #(.width(16)) Accumulator (.D(ALU_ac_load), .en(ADD), .Q(AC), .clk(CLOCK));  // open: clr

  // Other names for the same wires on the sheet: DR[15:0] = {I, OPCODE, Address_Part_of_Instruction}
endmodule

module ALU (
  input  [15:0] AC,
  input  [15:0] DR,
  output [15:0] AC_Load
);

  Adder #(.width(16)) adder_1 (.a(AC), .b(DR), .out(AC_Load));  // open: cin, cout
endmodule

module Incrementor (
  input  [6:0] CAR,
  output [6:0] CAR___1
);

  Adder #(.width(7)) adder_1 (.a(CAR), .b(7'b0000001), .out(CAR___1));  // open: cin, cout
endmodule

module CAR_Logic (
  input  [1:0] BR,
  input  CD_Logic,
  output [1:0] CAR_MUX,
  output SBR_Load
);

  wire and_1_out, and_2_out, not_1_out;

  not not_1 (not_1_out, BR[1]);
  and and_1 (and_1_out, BR[1], BR[0]);
  and and_2 (and_2_out, not_1_out, CD_Logic);
  and and_3 (SBR_Load, not_1_out, BR[0], CD_Logic);
  or or_1 (CAR_MUX[0], and_1_out, and_2_out);

  assign CAR_MUX[1] = BR[1];
endmodule
