// Logisim project Division_Algorithm.circ as structural Verilog: 1 circuit, main circuit main
module main (
  input  [9:0] AQ,
  input  [4:0] B,
  output [4:0] out_3,
  output [4:0] out_4,
  output E,
  output [4:0] A,
  output [4:0] Q_f
);

  wire adder_1_cout, adder_2_cout, and_1_out, and_2_out, and_4_out, and_5_out, C1, C2, comparator_2_eq, CP,
       EAld, not_2_out, not_3_out, not_4_out, not_5_out, or_1_out, or_2_out, or_4_out, Qld, Qnld, S1, S2, S3,
       sh, shift_register_2_out, shift_register_3_out, shift_register_4_out, shl, val_E;
  wire [1:0] counter_2_q;
  wire [3:0] counter_1_q;
  wire [4:0] adder_1_out, adder_2_out, not_1_out, val_A;

  Shift_Register #(.length(1)) shift_register_1 (
    .shift(shl), .in(shift_register_2_out), .clk(CP), .load(EAld), .d0(val_E), .q0(E));  // open: out, clr
  assign not_1_out = ~B;  // NOT_Gate not_1, 5 bits wide
  Adder #(.width(5)) adder_1 (.a(A), .b(not_1_out), .out(adder_1_out), .cin(1'b1), .cout(adder_1_cout));
  Shift_Register #(.length(5)) shift_register_2 (
    .shift(shl), .in(shift_register_4_out), .clk(CP), .out(shift_register_2_out), .load(EAld), .d0(val_A[0]),
    .q0(A[0]), .d1(val_A[1]), .q1(A[1]), .d2(val_A[2]), .q2(A[2]), .d3(val_A[3]), .q3(A[3]), .d4(val_A[4]),
    .q4(A[4]));  // open: clr
  Comparator #(.width(1)) comparator_1 (.a(E), .b(1'b1), .gt(C2), .eq(C1));  // open: lt
  assign val_E = Qld ? 1'b0 : 1'bz;  // Controlled_Buffer controlled_buffer_1
  assign val_A = Qld ? AQ[9:5] : 5'bz;  // Controlled_Buffer controlled_buffer_2
  assign val_A = S2 ? adder_1_out : 5'bz;  // Controlled_Buffer controlled_buffer_3
  assign val_E = S2 ? adder_1_cout : 1'bz;  // Controlled_Buffer controlled_buffer_4
  or or_1 (or_1_out, val_E, AQ[0]);
  Shift_Register #(.length(1)) shift_register_3 (
    .shift(shl), .in(1'b0), .clk(CP), .out(shift_register_3_out), .load(Qnld), .d0(or_1_out), .q0(Q_f[0]));  // open: clr
  Shift_Register #(.length(4)) shift_register_4 (
    .shift(shl), .in(shift_register_3_out), .clk(CP), .out(shift_register_4_out), .load(Qld), .d0(AQ[1]),
    .q0(Q_f[1]), .d1(AQ[2]), .q1(Q_f[2]), .d2(AQ[3]), .q2(Q_f[3]), .d3(AQ[4]), .q3(Q_f[4]));  // open: clr
  Clock clock_1 (.out(CP));
  Adder #(.width(5)) adder_2 (.a(A), .b(B), .out(adder_2_out), .cout(adder_2_cout));  // open: cin
  and and_1 (and_1_out, C1, S3);
  and and_2 (and_2_out, C2, S3);
  assign val_E = and_1_out ? 1'b1 : 1'bz;  // Controlled_Buffer controlled_buffer_5
  assign val_A = and_2_out ? adder_2_out : 5'bz;  // Controlled_Buffer controlled_buffer_6
  assign val_E = and_2_out ? adder_2_cout : 1'bz;  // Controlled_Buffer controlled_buffer_7
  not not_2 (not_2_out, 1'b1);
  Multiplexer #(.select(4)) multiplexer_1 (
    .in0(1'b1), .in1(not_2_out), .in2(not_2_out), .in3(not_2_out), .in4(not_2_out), .in5(not_2_out),
    .in6(not_2_out), .in7(not_2_out), .in8(not_2_out), .in9(not_2_out), .in10(not_2_out), .in11(not_2_out),
    .in12(not_2_out), .in13(not_2_out), .in14(not_2_out), .in15(not_2_out), .out(Qld), .sel(counter_1_q));  // open: en
  Counter #(.width(4), .max('hf)) counter_1 (.Q(counter_1_q), .clk(CP));  // open: load, D, count, carry, clr
  not not_3 (not_3_out, S2);
  not not_4 (not_4_out, S3);
  and and_3 (sh, S1, not_3_out, not_4_out);
  Counter #(.width(2), .max('h3)) counter_2 (.Q(counter_2_q), .clk(CP), .clr(or_2_out));  // open: load, D, count, carry
  or or_2 (or_2_out, Qld, comparator_2_eq);
  Comparator #(.width(2)) comparator_2 (.a(counter_2_q), .b(2'b11), .eq(comparator_2_eq));  // open: gt, lt
  not not_5 (not_5_out, Qld);
  and and_4 (and_4_out, C1, S3);
  and and_5 (and_5_out, S3, C2);
  Decoder #(.select(2)) decoder_1 (.out0(S1), .out1(S2), .out2(S3), .sel(counter_2_q));  // open: out3, en
  and and_6 (shl, not_5_out, sh);
  or or_3 (Qnld, Qld, and_4_out);
  or or_4 (or_4_out, S2, and_5_out);
  or or_5 (EAld, Qld, or_4_out);

  assign out_3 = AQ[9:5];
  assign out_4 = AQ[4:0];

  // Other names for the same wires on the sheet: Q[4:0] = AQ[4:0]; A_f[4:0] = AQ[9:5]; val_Qn = val_E
endmodule
