// Logisim project Electronic Voting Machine.circ as structural Verilog: 3 circuits, main circuit main
module main (
  input  in_1,
  input  in_2,
  input  in_3,
  input  in_4,
  input  [1:0] in_5,
  input  in_6,
  input  in_7
);

  wire _3_qn, and_1_out, and_2_out, and_3_out, and_4_out, and_5_out, and_6_out, clock_1_out, clock_2_out,
       counter_to_bcd_1_a, counter_to_bcd_1_b, counter_to_bcd_1_c, counter_to_bcd_1_d, counter_to_bcd_1_e,
       counter_to_bcd_2_a, counter_to_bcd_2_b, counter_to_bcd_2_c, counter_to_bcd_2_d, counter_to_bcd_2_e,
       counter_to_bcd_3_a, counter_to_bcd_3_b, counter_to_bcd_3_c, counter_to_bcd_3_d, counter_to_bcd_3_e,
       counter_to_bcd_4_a, counter_to_bcd_4_b, counter_to_bcd_4_c, counter_to_bcd_4_d, counter_to_bcd_4_e,
       decoder_1_out0, decoder_1_out1, decoder_1_out2, decoder_1_out3, demultiplexer_1_out0,
       demultiplexer_1_out1, demultiplexer_1_out2, demultiplexer_1_out3, demultiplexer_1_out4,
       demultiplexer_1_out5, demultiplexer_1_out6, demultiplexer_1_out7, demultiplexer_1_out8,
       demultiplexer_1_out9, demultiplexer_1_out10, demultiplexer_1_out11, demultiplexer_1_out12,
       demultiplexer_1_out13, demultiplexer_1_out14, demultiplexer_1_out15, n7_segment_1_out_5,
       n7_segment_1_out_6, n7_segment_1_out_7, n7_segment_1_out_8, n7_segment_1_out_9, n7_segment_1_out_10,
       n7_segment_1_out_11, n7_segment_2_out_5, n7_segment_2_out_6, n7_segment_2_out_7, n7_segment_2_out_8,
       n7_segment_2_out_9, n7_segment_2_out_10, n7_segment_2_out_11, n7_segment_3_out_5, n7_segment_3_out_6,
       n7_segment_3_out_7, n7_segment_3_out_8, n7_segment_3_out_9, n7_segment_3_out_10, n7_segment_3_out_11,
       n7_segment_4_out_5, n7_segment_4_out_6, n7_segment_4_out_7, n7_segment_4_out_8, n7_segment_4_out_9,
       n7_segment_4_out_10, n7_segment_4_out_11, n7_segment_5_out_5, n7_segment_5_out_6, n7_segment_5_out_7,
       n7_segment_5_out_8, n7_segment_5_out_9, n7_segment_5_out_10, n7_segment_5_out_11, n7_segment_6_out_5,
       n7_segment_6_out_6, n7_segment_6_out_7, n7_segment_6_out_8, n7_segment_6_out_9, n7_segment_6_out_10,
       n7_segment_6_out_11, n7_segment_7_out_5, n7_segment_7_out_6, n7_segment_7_out_7, n7_segment_7_out_8,
       n7_segment_7_out_9, n7_segment_7_out_10, n7_segment_7_out_11, n7_segment_8_out_5, n7_segment_8_out_6,
       n7_segment_8_out_7, n7_segment_8_out_8, n7_segment_8_out_9, n7_segment_8_out_10, n7_segment_8_out_11;
  wire [1:0] multiplexer_1_out;
  wire [3:0] _1_q;

  and and_1 (and_1_out, clock_1_out, decoder_1_out0);
  Counter_To_BCD counter_to_bcd_1 (
    .INPUT_1(decoder_1_out0), .A(counter_to_bcd_1_a), .B(counter_to_bcd_1_b), .C(counter_to_bcd_1_c),
    .D(counter_to_bcd_1_d), .E(counter_to_bcd_1_e), .in_1(and_1_out));
  _7_Segment u_7_segment_1 (
    .W(in_3), .X(in_3), .Y(in_3), .Z(counter_to_bcd_1_a), .out_5(n7_segment_1_out_5),
    .out_6(n7_segment_1_out_6), .out_7(n7_segment_1_out_7), .out_8(n7_segment_1_out_8),
    .out_9(n7_segment_1_out_9), .out_10(n7_segment_1_out_10), .out_11(n7_segment_1_out_11));
  and and_2 (and_2_out, clock_1_out, decoder_1_out2);
  Counter_To_BCD counter_to_bcd_2 (
    .INPUT_1(decoder_1_out2), .A(counter_to_bcd_2_a), .B(counter_to_bcd_2_b), .C(counter_to_bcd_2_c),
    .D(counter_to_bcd_2_d), .E(counter_to_bcd_2_e), .in_1(and_2_out));
  _7_Segment u_7_segment_2 (
    .W(in_7), .X(in_7), .Y(in_7), .Z(counter_to_bcd_2_a), .out_5(n7_segment_2_out_5),
    .out_6(n7_segment_2_out_6), .out_7(n7_segment_2_out_7), .out_8(n7_segment_2_out_8),
    .out_9(n7_segment_2_out_9), .out_10(n7_segment_2_out_10), .out_11(n7_segment_2_out_11));
  Clock clock_1 (.out(clock_1_out));
  _7_Segment_Display u_7_segment_display_1 (
    .g(n7_segment_1_out_8), .f(n7_segment_1_out_7), .a(n7_segment_1_out_6), .b(n7_segment_1_out_5),
    .e(n7_segment_1_out_11), .d(n7_segment_1_out_10), .c(n7_segment_1_out_9));  // open: dp
  _7_Segment_Display u_7_segment_display_2 (
    .g(n7_segment_2_out_8), .f(n7_segment_2_out_7), .a(n7_segment_2_out_6), .b(n7_segment_2_out_5),
    .e(n7_segment_2_out_11), .d(n7_segment_2_out_10), .c(n7_segment_2_out_9));  // open: dp
  _7_Segment_Display u_7_segment_display_3 (
    .g(n7_segment_3_out_8), .f(n7_segment_3_out_7), .a(n7_segment_3_out_6), .b(n7_segment_3_out_5),
    .e(n7_segment_3_out_11), .d(n7_segment_3_out_10), .c(n7_segment_3_out_9));  // open: dp
  _7_Segment_Display u_7_segment_display_4 (
    .g(n7_segment_4_out_8), .f(n7_segment_4_out_7), .a(n7_segment_4_out_6), .b(n7_segment_4_out_5),
    .e(n7_segment_4_out_11), .d(n7_segment_4_out_10), .c(n7_segment_4_out_9));  // open: dp
  Decoder #(.select(2)) decoder_1 (
    .out0(decoder_1_out0), .out1(decoder_1_out1), .out2(decoder_1_out2), .out3(decoder_1_out3),
    .sel(multiplexer_1_out));  // open: en
  _7_Segment u_7_segment_3 (
    .W(counter_to_bcd_1_b), .X(counter_to_bcd_1_c), .Y(counter_to_bcd_1_d), .Z(counter_to_bcd_1_e),
    .out_5(n7_segment_3_out_5), .out_6(n7_segment_3_out_6), .out_7(n7_segment_3_out_7),
    .out_8(n7_segment_3_out_8), .out_9(n7_segment_3_out_9), .out_10(n7_segment_3_out_10),
    .out_11(n7_segment_3_out_11));
  _7_Segment u_7_segment_4 (
    .W(counter_to_bcd_2_b), .X(counter_to_bcd_2_c), .Y(counter_to_bcd_2_d), .Z(counter_to_bcd_2_e),
    .out_5(n7_segment_4_out_5), .out_6(n7_segment_4_out_6), .out_7(n7_segment_4_out_7),
    .out_8(n7_segment_4_out_8), .out_9(n7_segment_4_out_9), .out_10(n7_segment_4_out_10),
    .out_11(n7_segment_4_out_11));
  and and_3 (and_3_out, clock_1_out, decoder_1_out1);
  Counter_To_BCD counter_to_bcd_3 (
    .INPUT_1(decoder_1_out1), .A(counter_to_bcd_3_a), .B(counter_to_bcd_3_b), .C(counter_to_bcd_3_c),
    .D(counter_to_bcd_3_d), .E(counter_to_bcd_3_e), .in_1(and_3_out));
  _7_Segment u_7_segment_5 (
    .W(in_4), .X(in_4), .Y(in_4), .Z(counter_to_bcd_3_a), .out_5(n7_segment_5_out_5),
    .out_6(n7_segment_5_out_6), .out_7(n7_segment_5_out_7), .out_8(n7_segment_5_out_8),
    .out_9(n7_segment_5_out_9), .out_10(n7_segment_5_out_10), .out_11(n7_segment_5_out_11));
  and and_4 (and_4_out, clock_1_out, decoder_1_out3);
  Counter_To_BCD counter_to_bcd_4 (
    .INPUT_1(decoder_1_out3), .A(counter_to_bcd_4_a), .B(counter_to_bcd_4_b), .C(counter_to_bcd_4_c),
    .D(counter_to_bcd_4_d), .E(counter_to_bcd_4_e), .in_1(and_4_out));
  _7_Segment u_7_segment_6 (
    .W(in_6), .X(in_6), .Y(in_6), .Z(counter_to_bcd_4_a), .out_5(n7_segment_6_out_5),
    .out_6(n7_segment_6_out_6), .out_7(n7_segment_6_out_7), .out_8(n7_segment_6_out_8),
    .out_9(n7_segment_6_out_9), .out_10(n7_segment_6_out_10), .out_11(n7_segment_6_out_11));
  _7_Segment_Display u_7_segment_display_5 (
    .g(n7_segment_5_out_8), .f(n7_segment_5_out_7), .a(n7_segment_5_out_6), .b(n7_segment_5_out_5),
    .e(n7_segment_5_out_11), .d(n7_segment_5_out_10), .c(n7_segment_5_out_9));  // open: dp
  _7_Segment_Display u_7_segment_display_6 (
    .g(n7_segment_6_out_8), .f(n7_segment_6_out_7), .a(n7_segment_6_out_6), .b(n7_segment_6_out_5),
    .e(n7_segment_6_out_11), .d(n7_segment_6_out_10), .c(n7_segment_6_out_9));  // open: dp
  _7_Segment_Display u_7_segment_display_7 (
    .g(n7_segment_7_out_8), .f(n7_segment_7_out_7), .a(n7_segment_7_out_6), .b(n7_segment_7_out_5),
    .e(n7_segment_7_out_11), .d(n7_segment_7_out_10), .c(n7_segment_7_out_9));  // open: dp
  _7_Segment_Display u_7_segment_display_8 (
    .g(n7_segment_8_out_8), .f(n7_segment_8_out_7), .a(n7_segment_8_out_6), .b(n7_segment_8_out_5),
    .e(n7_segment_8_out_11), .d(n7_segment_8_out_10), .c(n7_segment_8_out_9));  // open: dp
  _7_Segment u_7_segment_7 (
    .W(counter_to_bcd_3_b), .X(counter_to_bcd_3_c), .Y(counter_to_bcd_3_d), .Z(counter_to_bcd_3_e),
    .out_5(n7_segment_7_out_5), .out_6(n7_segment_7_out_6), .out_7(n7_segment_7_out_7),
    .out_8(n7_segment_7_out_8), .out_9(n7_segment_7_out_9), .out_10(n7_segment_7_out_10),
    .out_11(n7_segment_7_out_11));
  LED led_1 (.in(clock_1_out));
  _7_Segment u_7_segment_8 (
    .W(counter_to_bcd_4_b), .X(counter_to_bcd_4_c), .Y(counter_to_bcd_4_d), .Z(counter_to_bcd_4_e),
    .out_5(n7_segment_8_out_5), .out_6(n7_segment_8_out_6), .out_7(n7_segment_8_out_7),
    .out_8(n7_segment_8_out_8), .out_9(n7_segment_8_out_9), .out_10(n7_segment_8_out_10),
    .out_11(n7_segment_8_out_11));
  LED led_2 (.in(demultiplexer_1_out0));
  LED led_3 (.in(demultiplexer_1_out1));
  LED led_4 (.in(demultiplexer_1_out2));
  LED led_5 (.in(demultiplexer_1_out3));
  LED led_6 (.in(demultiplexer_1_out4));
  LED led_7 (.in(demultiplexer_1_out5));
  LED led_8 (.in(demultiplexer_1_out6));
  LED led_9 (.in(demultiplexer_1_out7));
  LED led_10 (.in(demultiplexer_1_out8));
  LED led_11 (.in(demultiplexer_1_out9));
  LED led_12 (.in(demultiplexer_1_out10));
  LED led_13 (.in(demultiplexer_1_out11));
  LED led_14 (.in(demultiplexer_1_out12));
  LED led_15 (.in(demultiplexer_1_out13));
  LED led_16 (.in(demultiplexer_1_out14));
  LED led_17 (.in(demultiplexer_1_out15));
  Multiplexer #(.select(4), .width(2)) multiplexer_1 (
    .in0(in_5), .in1(in_5), .in2(in_5), .in3(in_5), .in4(in_5), .in5(in_5), .in6(in_5), .in7(in_5),
    .in8(in_5), .in9(in_5), .in10(in_5), .in11(in_5), .in12(in_5), .in13(in_5), .in14(in_5), .in15(in_5),
    .out(multiplexer_1_out), .sel({_1_q[0], _1_q[1], _1_q[2], _1_q[3]}));  // open: en
  and and_5 (and_5_out, _1_q[2], and_6_out);
  T_Flip_Flop _4 (.clk(clock_2_out), .T(and_5_out), .Q(_1_q[3]));  // open: Qn, preset, reset, en
  Demultiplexer #(.select(4)) demultiplexer_1 (
    .out0(demultiplexer_1_out0), .out1(demultiplexer_1_out1), .out2(demultiplexer_1_out2),
    .out3(demultiplexer_1_out3), .out4(demultiplexer_1_out4), .out5(demultiplexer_1_out5),
    .out6(demultiplexer_1_out6), .out7(demultiplexer_1_out7), .out8(demultiplexer_1_out8),
    .out9(demultiplexer_1_out9), .out10(demultiplexer_1_out10), .out11(demultiplexer_1_out11),
    .out12(demultiplexer_1_out12), .out13(demultiplexer_1_out13), .out14(demultiplexer_1_out14),
    .out15(demultiplexer_1_out15), .in(in_2), .sel(_1_q));  // open: en
  T_Flip_Flop _3 (.clk(clock_2_out), .T(and_6_out), .Q(_1_q[2]), .Qn(_3_qn));  // open: preset, reset, en
  and and_6 (and_6_out, _1_q[0], _1_q[1]);
  T_Flip_Flop _2 (.clk(clock_2_out), .T(_1_q[0]), .Q(_1_q[1]));  // open: Qn, preset, reset, en
  T_Flip_Flop _1 (.clk(clock_2_out), .T(in_1), .Q(_1_q[0]));  // open: Qn, preset, reset, en
  Clock clock_2 (.out(clock_2_out));

  // Notes on the sheet:
  //   party 1
  //   party 3
  //   party 2
  //   Other
  //   Political Party 1
  //   Political Party 2
  //   Political Party 3
  //   Other
  //   00
  //   01
  //   10
  //   11
endmodule

module _7_Segment (
  input  W,
  input  X,
  input  Y,
  input  Z,
  output out_5,
  output out_6,
  output out_7,
  output out_8,
  output out_9,
  output out_10,
  output out_11
);

  wire and_1_out, and_2_out, and_3_out, and_4_out, and_5_out, and_6_out, and_7_out, and_9_out, not_1_out,
       not_2_out, not_3_out, not_4_out, not_5_out, not_6_out, not_7_out, or_5_out, xnor_1_out, xnor_2_out,
       xnor_3_out, xor_1_out;

  not not_1 (not_1_out, Y);
  not not_2 (not_2_out, Z);
  not not_3 (not_3_out, X);
  xnor xnor_1 (xnor_1_out, Z, X);
  and and_1 (and_1_out, not_1_out, not_2_out);
  xnor xnor_2 (xnor_2_out, Z, Y);
  or or_1 (out_6, Y, W, xnor_1_out);
  and and_2 (and_2_out, X, not_2_out);
  or or_2 (out_9, W, not_1_out, X, Z);
  and and_3 (and_3_out, not_1_out, Z);
  not not_4 (not_4_out, X);
  or or_3 (out_5, xnor_2_out, not_3_out, W);
  not not_5 (not_5_out, Z);
  and and_4 (and_4_out, not_1_out, X);
  xnor xnor_3 (xnor_3_out, and_3_out, X);
  and and_5 (and_5_out, Y, not_2_out);
  or or_4 (out_10, W, xnor_3_out, and_5_out);
  or or_5 (or_5_out, not_4_out, Y);
  not not_6 (not_6_out, W);
  not not_7 (not_7_out, not_3_out);
  and and_6 (and_6_out, not_3_out, W);
  and and_7 (and_7_out, not_5_out, Y);
  or or_6 (out_7, W, and_4_out, and_2_out, and_1_out);
  and and_8 (out_11, or_5_out, not_2_out);
  and and_9 (and_9_out, not_6_out, xor_1_out);
  xor xor_1 (xor_1_out, not_7_out, Y);
  or or_7 (out_8, and_9_out, and_6_out, and_7_out);
  _7_Segment_Display u_7_segment_display_1 (
    .g(out_8), .f(out_7), .a(out_6), .b(out_5), .e(out_11), .d(out_10), .c(out_9));  // open: dp

  // Notes on the sheet:
  //   B
  //   D
  //    7 SEGMENT DECODER
  //   C
  //   A
  //   E
  //   F
  //   G
endmodule

module Counter_To_BCD (
  input  in_1,
  input  INPUT_1,
  output A,
  output B,
  output C,
  output D,
  output E
);

  wire _2_q, _2_qn, _3_q, _3_qn, _4_q, _4_qn, and_1_out, and_2_out, and_3_out, and_4_out, and_6_out,
       and_7_out, and_8_out, and_9_out;

  and and_1 (and_1_out, _3_q, and_4_out);
  and and_2 (and_2_out, _4_q, _3_q);
  T_Flip_Flop _4 (.clk(in_1), .T(and_1_out), .Q(_4_q), .Qn(_4_qn));  // open: preset, reset, en
  and and_3 (and_3_out, _4_q, _2_q);
  or or_1 (A, and_2_out, and_3_out);
  and and_4 (and_4_out, E, _2_q);
  T_Flip_Flop _3 (.clk(in_1), .T(and_4_out), .Q(_3_q), .Qn(_3_qn));  // open: preset, reset, en
  and and_5 (B, _4_q, _3_qn, _2_qn);
  T_Flip_Flop _2 (.clk(in_1), .T(E), .Q(_2_q), .Qn(_2_qn));  // open: preset, reset, en
  T_Flip_Flop _1 (.clk(in_1), .T(INPUT_1), .Q(E));  // open: Qn, preset, reset, en
  and and_6 (and_6_out, _3_q, _2_q);
  and and_7 (and_7_out, _4_qn, _3_q);
  or or_2 (C, and_6_out, and_7_out);
  and and_8 (and_8_out, _4_qn, _2_q);
  or or_3 (D, and_8_out, and_9_out);
  and and_9 (and_9_out, _4_q, _3_q, _2_qn);
endmodule
