// Logisim project Instruction_Cycle(AND-ADD-BUN-SKI).circ as structural Verilog: 7 circuits, main circuit Common Bus System
module Common_Bus_System (
  output [3:0] SC_Count
);

  wire adder_and_logic_1_e_input, Clock_Pulse_out, control_unit_1_ac_load, control_unit_1_add_signal,
       control_unit_1_and_signal, control_unit_1_ar_load, control_unit_1_dr_load, control_unit_1_ir_load,
       control_unit_1_pc_increment, control_unit_1_pc_load, FGI_q, not_1_out;
  wire [2:0] control_unit_1_common_bus_selection;
  wire [11:0] Address_Register_q, n16_12bit_converter_1_output_12_bit, Program_Counter_q;
  wire [15:0] Accumulator_q, adder_and_logic_1_ac_load_input, Data_Register_q, Instruction_Register_q,
       multiplexer_1_out, n12_16bit_converter_1_output_16_bits, n12_16bit_converter_2_output_16_bits,
       rom_1_data;

  J_K_Flip_Flop FGI (.Q(FGI_q));  // open: J, clk, K, Qn, preset, en, reset
  Button Clock_Pulse (.out(Clock_Pulse_out));
  Control_Unit control_unit_1 (
    .Instruction_Register(Instruction_Register_q), .FGI_bit(FGI_q), .SC_Clock(Clock_Pulse_out),
    .Common_Bus_Selection(control_unit_1_common_bus_selection), .SC_Count(SC_Count),
    .AR_Load(control_unit_1_ar_load), .PC_Load(control_unit_1_pc_load),
    .PC_Increment(control_unit_1_pc_increment), .DR_Load(control_unit_1_dr_load),
    .AC_Load(control_unit_1_ac_load), .IR_Load(control_unit_1_ir_load),
    .AND_Signal(control_unit_1_and_signal), .ADD_Signal(control_unit_1_add_signal));
  Adder_and_Logic adder_and_logic_1 (
    .ADD_Signal(control_unit_1_add_signal), .AND_Signal(control_unit_1_and_signal),
    .Data_Register(Data_Register_q), .Accumulator(Accumulator_q),
    .AC_Load_Input(adder_and_logic_1_ac_load_input), .E_Input(adder_and_logic_1_e_input));
  not not_1 (not_1_out, adder_and_logic_1_e_input);
  _16_12bit_Converter u_16_12bit_converter_1 (
    .Input_16_bit(multiplexer_1_out), .Output_12_bit(n16_12bit_converter_1_output_12_bit));
  Register #(.width(12)) Address_Register (
    .D(n16_12bit_converter_1_output_12_bit), .en(control_unit_1_ar_load), .Q(Address_Register_q),
    .clk(Clock_Pulse_out));  // open: clr
  Counter #(.width(12), .max('hfff)) Program_Counter (
    .load(control_unit_1_pc_load), .D(n16_12bit_converter_1_output_12_bit),
    .count(control_unit_1_pc_increment), .Q(Program_Counter_q), .clk(Clock_Pulse_out));  // open: carry, clr
  Register #(.width(16)) Data_Register (
    .D(multiplexer_1_out), .en(control_unit_1_dr_load), .Q(Data_Register_q), .clk(Clock_Pulse_out));  // open: clr
  J_K_Flip_Flop E (
    .J(adder_and_logic_1_e_input), .clk(Clock_Pulse_out), .K(not_1_out), .en(control_unit_1_add_signal));  // open: Q, Qn, preset, reset
  Register #(.width(16)) Accumulator (
    .D(adder_and_logic_1_ac_load_input), .en(control_unit_1_ac_load), .Q(Accumulator_q), .clk(Clock_Pulse_out));  // open: clr
  Register #(.width(16)) Instruction_Register (
    .D(multiplexer_1_out), .en(control_unit_1_ir_load), .Q(Instruction_Register_q), .clk(Clock_Pulse_out));  // open: clr
  ROM #(.addrWidth(12), .dataWidth(16)) rom_1 (.addr(Address_Register_q), .data(rom_1_data));  // open: sel
  _12_16bit_Converter u_12_16bit_converter_1 (
    .Input_12_bits(Address_Register_q), .Output_16_Bits(n12_16bit_converter_1_output_16_bits));
  _12_16bit_Converter u_12_16bit_converter_2 (
    .Input_12_bits(Program_Counter_q), .Output_16_Bits(n12_16bit_converter_2_output_16_bits));
  Multiplexer #(.select(3), .width(16)) multiplexer_1 (
    .in1(n12_16bit_converter_1_output_16_bits), .in2(n12_16bit_converter_2_output_16_bits),
    .in3(Data_Register_q), .in4(Accumulator_q), .in5(Instruction_Register_q), .in7(rom_1_data),
    .out(multiplexer_1_out), .sel(control_unit_1_common_bus_selection));  // open: in0, in6, en

  // Notes on the sheet:
  //   contents of rom_1 (hex, n*v repeats v):
  //   abf 123b 9081 8137 f200 c059 4f11 122*0 c3d0 16*0 f1fa 164*0 8092 259*0 abcd 404*0 f1f2 1774*0 ffff
  //   1105*0 c132
endmodule

module Control_Unit (
  input  [15:0] Instruction_Register,
  input  FGI_bit,
  input  SC_Clock,
  output [2:0] Common_Bus_Selection,
  output AR_Load,
  output PC_Load,
  output PC_Increment,
  output DR_Load,
  output AC_Load,
  output IR_Load,
  output AND_Signal,
  output ADD_Signal,
  output [3:0] SC_Count
);

  wire control_logics_1_sc_clear, I_q, not_1_out, not_2_out;
  wire [7:0] decoder_1_out0;
  wire [15:0] decoder_2_out0;

  not not_1 (not_1_out, control_logics_1_sc_clear);
  J_K_Flip_Flop I (
    .J(Instruction_Register[15]), .clk(SC_Clock), .K(not_2_out), .Q(I_q));  // open: Qn, preset, en, reset
  not not_2 (not_2_out, Instruction_Register[15]);
  Counter #(.width(4), .max('hf)) Sequence_Counter (
    .load(control_logics_1_sc_clear), .D(4'b0000), .count(not_1_out), .Q(SC_Count), .clk(SC_Clock));  // open: carry, clr
  Decoder #(.select(3), .enable("false")) decoder_1 (
    .out0(decoder_1_out0[0]), .out1(decoder_1_out0[1]), .out2(decoder_1_out0[2]), .out3(decoder_1_out0[3]),
    .out4(decoder_1_out0[4]), .out5(decoder_1_out0[5]), .out6(decoder_1_out0[6]), .out7(decoder_1_out0[7]),
    .sel(Instruction_Register[14:12]));
  Decoder #(.select(4), .enable("false")) decoder_2 (
    .out0(decoder_2_out0[0]), .out1(decoder_2_out0[1]), .out2(decoder_2_out0[2]), .out3(decoder_2_out0[3]),
    .out4(decoder_2_out0[4]), .out5(decoder_2_out0[5]), .out6(decoder_2_out0[6]), .out7(decoder_2_out0[7]),
    .out8(decoder_2_out0[8]), .out9(decoder_2_out0[9]), .out10(decoder_2_out0[10]),
    .out11(decoder_2_out0[11]), .out12(decoder_2_out0[12]), .out13(decoder_2_out0[13]),
    .out14(decoder_2_out0[14]), .out15(decoder_2_out0[15]), .sel(SC_Count));
  Control_Logic_Gates control_logics_1 (
    .Address(Instruction_Register[11:0]), .Operation_Code(decoder_1_out0), .Indirect_Bit(I_q),
    .Timing_Signals(decoder_2_out0), .FGI_bit(FGI_bit), .IR_Load(IR_Load),
    .Common_Bus_Selection(Common_Bus_Selection), .AR_Load(AR_Load), .PC_Load(PC_Load),
    .PC_Increment(PC_Increment), .DR_Load(DR_Load), .AC_Load(AC_Load), .ADD_Signal(ADD_Signal),
    .AND_Signal(AND_Signal), .SC_Clear(control_logics_1_sc_clear));  // open: Memory_Read
endmodule

module Control_Logic_Gates (
  input  [11:0] Address,
  input  [7:0] Operation_Code,
  input  FGI_bit,
  input  Indirect_Bit,
  input  [15:0] Timing_Signals,
  output [2:0] Common_Bus_Selection,
  output Memory_Read,
  output AR_Load,
  output PC_Load,
  output PC_Increment,
  output DR_Load,
  output AND_Signal,
  output AC_Load,
  output ADD_Signal,
  output IR_Load,
  output SC_Clear
);

  wire and_1_out, and_2_out, and_4_out, and_5_out, and_6_out, and_7_out, and_8_out, and_9_out, and_10_out,
       and_11_out, not_1_out;

  not not_1 (not_1_out, Operation_Code[7]);
  and and_1 (and_1_out, Operation_Code[0], Timing_Signals[5]);
  and and_2 (and_2_out, Timing_Signals[5], Operation_Code[1]);
  and and_3 (PC_Load, Operation_Code[4], Timing_Signals[4]);
  and and_4 (and_4_out, not_1_out, Indirect_Bit, Timing_Signals[3]);
  and and_5 (and_5_out, Operation_Code[0], Timing_Signals[4]);
  and and_6 (and_6_out, Timing_Signals[4], Operation_Code[1]);
  and and_7 (and_7_out, Operation_Code[4], Timing_Signals[4]);
  and and_8 (and_8_out, Operation_Code[7], Indirect_Bit, Timing_Signals[3]);
  or or_1 (Memory_Read, Timing_Signals[1], and_4_out, and_5_out, and_6_out);
  and and_9 (and_9_out, Operation_Code[7], Indirect_Bit, Timing_Signals[3], Address[9], FGI_bit);
  and and_10 (and_10_out, Operation_Code[0], Timing_Signals[4]);
  and and_11 (and_11_out, Timing_Signals[4], Operation_Code[1]);
  and and_12 (AND_Signal, Operation_Code[0], Timing_Signals[5]);
  and and_13 (ADD_Signal, Timing_Signals[5], Operation_Code[1]);
  or or_2 (SC_Clear, and_1_out, and_2_out, and_7_out, and_8_out);
  Priority_Encoder priority_encoder_1 (
    .in1(PC_Load), .in2(Timing_Signals[0]), .in5(Timing_Signals[2]), .in7(Memory_Read),
    .out(Common_Bus_Selection));  // open: in0, in3, in4, in6, en_in, gs, en_out
  or or_3 (AR_Load, Timing_Signals[0], and_4_out, Timing_Signals[2]);
  or or_4 (PC_Increment, Timing_Signals[1], and_9_out);
  or or_5 (DR_Load, and_10_out, and_11_out);
  or or_6 (AC_Load, AND_Signal, ADD_Signal);

  assign IR_Load = Timing_Signals[1];

  // Other names for the same wires on the sheet: B0 = Address[0]; B1 = Address[1]; B2 = Address[2]; B3 = Address[3];
  //   B4 = Address[4]; B5 = Address[5]; B6 = Address[6]; B7 = Address[7]; B8 = Address[8]; B9 = Address[9];
  //   B10 = Address[10]; B11 = Address[11]; FGI = FGI_bit; I = Indirect_Bit; D0 = Operation_Code[0];
  //   D1 = Operation_Code[1]; D2 = Operation_Code[2]; D3 = Operation_Code[3]; D4 = Operation_Code[4];
  //   D5 = Operation_Code[5]; D6 = Operation_Code[6]; D7 = Operation_Code[7]; T0 = Timing_Signals[0];
  //   T1 = Timing_Signals[1]; T2 = Timing_Signals[2]; T3 = Timing_Signals[3]; T4 = Timing_Signals[4];
  //   T5 = Timing_Signals[5]; T6 = Timing_Signals[6]; T7 = Timing_Signals[7]; T8 = Timing_Signals[8];
  //   T9 = Timing_Signals[9]; T10 = Timing_Signals[10]; T11 = Timing_Signals[11]; T12 = Timing_Signals[12];
  //   T13 = Timing_Signals[13]; T14 = Timing_Signals[14]; T15 = Timing_Signals[15]
endmodule

// ALU
module Adder_and_Logic (
  input  ADD_Signal,
  input  AND_Signal,
  input  [15:0] Data_Register,
  input  [15:0] Accumulator,
  output E_Input,
  output [15:0] AC_Load_Input
);

  wire adder_1_cout;
  wire [15:0] adder_1_out, and_1_out, and_3_out, and_4_out, n1_16bit_converter_1_output,
       n1_16bit_converter_2_output;

  _1_16bit_Converter u_1_16bit_converter_1 (.Input(ADD_Signal), .Output(n1_16bit_converter_1_output));
  _1_16bit_Converter u_1_16bit_converter_2 (.Input(AND_Signal), .Output(n1_16bit_converter_2_output));
  Adder #(.width(16)) adder_1 (
    .a(Data_Register), .b(Accumulator), .out(adder_1_out), .cout(adder_1_cout));  // open: cin
  assign and_1_out = Data_Register & Accumulator;  // AND_Gate and_1, 16 bits wide
  and and_2 (E_Input, ADD_Signal, adder_1_cout);
  assign and_3_out = adder_1_out & n1_16bit_converter_1_output;  // AND_Gate and_3, 16 bits wide
  assign and_4_out = and_1_out & n1_16bit_converter_2_output;  // AND_Gate and_4, 16 bits wide
  assign AC_Load_Input = and_3_out | and_4_out;  // OR_Gate or_1, 16 bits wide
endmodule

// 1-16
module _1_16bit_Converter (
  input  Input,
  output [15:0] Output
);


  assign Output = {16{Input}};
endmodule

// 12-16
module _12_16bit_Converter (
  input  [11:0] Input_12_bits,
  output [15:0] Output_16_Bits
);


  assign Output_16_Bits = {4'b0000, Input_12_bits};
endmodule

// 16-12
module _16_12bit_Converter (
  input  [15:0] Input_16_bit,
  output [11:0] Output_12_bit
);


  assign Output_12_bit = Input_16_bit[11:0];
endmodule
