// Logisim project Multiplication_Algorithm.circ as structural Verilog: 2 circuits, main circuit main
module main (
  input  in_1,
  input  in_2,
  input  in_3,
  input  in_4,
  input  in_5,
  input  in_6,
  input  in_7,
  input  in_8,
  input  in_9,
  input  A3,
  input  A2,
  input  A1,
  input  A0,
  output out_14,
  output out_15,
  output out_16,
  output out_17,
  output [7:0] out_18
);

  wire a1_shr, a2_shr, a_shr, AC_out, ACld, ADD, and_4_out, and_5_out, ashr, CP, ld, not_1_out, not_2_out,
       not_3_out, not_4_out, not_5_out, not_6_out, not_7_out, or_2_out, or_3_out, or_4_out, or_5_out, Qn_1,
       QR_out, QRld, SUB, xnor_2_out, xor_1_out, xor_2_out, xor_3_out, xor_4_out;
  wire [2:0] counter_1_q, undriven;

  Shift_Register #(.length(4)) BR (
    .clk(CP), .load(in_9), .d0(in_1), .d1(in_2), .d2(in_3), .d3(in_4));  // open: shift, in, out, clr, q0, q1, q2, q3
  and and_1 (ld, ACld, not_1_out);
  not not_1 (not_1_out, a_shr);
  or or_1 (a_shr, a2_shr, a1_shr);
  or or_2 (or_2_out, A3, out_17);
  or or_3 (or_3_out, A2, out_16);
  or or_4 (or_4_out, A1, out_15);
  or or_5 (or_5_out, A0, out_14);
  or or_6 (ACld, ADD, SUB);
  D_Flip_Flop d_ff_1 (.clk(CP), .D(ACld), .Q(a2_shr));  // open: Qn, preset, en, reset
  Shift_Register #(.length(4)) AC (
    .shift(a_shr), .in(out_18[7]), .clk(CP), .out(AC_out), .load(ld), .d0(or_2_out), .q0(out_18[7]),
    .d1(or_3_out), .q1(out_18[6]), .d2(or_4_out), .q2(out_18[5]), .d3(or_5_out), .q3(out_18[4]));  // open: clr
  not not_2 (not_2_out, out_18[0]);
  not not_3 (not_3_out, Qn_1);
  Shift_Register #(.length(4)) QR (
    .shift(a_shr), .in(AC_out), .clk(CP), .out(QR_out), .load(QRld), .d0(in_5), .q0(out_18[3]), .d1(in_6),
    .q1(out_18[2]), .d2(in_7), .q2(out_18[1]), .d3(in_8), .q3(out_18[0]));  // open: clr
  and and_2 (ADD, not_2_out, Qn_1);
  and and_3 (SUB, out_18[0], not_3_out);
  D_Flip_Flop u_Qn_1 (.clk(CP), .D(QR_out), .Q(Qn_1));  // open: Qn, preset, en, reset
  Clock clock_1 (.out(CP));
  xnor xnor_1 (a1_shr, out_18[0], Qn_1);
  xnor xnor_2 (xnor_2_out, out_18[0], Qn_1);
  not not_4 (not_4_out, ADD);
  Counter #(.width(3), .max('h7)) counter_1 (
    .D(undriven), .count(a_shr), .Q(counter_1_q), .clk(and_4_out));  // open: load, carry, clr
  buf and_4 (and_4_out, CP);  // AND_Gate
  and and_5 (and_5_out, not_4_out, SUB);
  not not_5 (not_5_out, counter_1_q[0]);
  not not_6 (not_6_out, counter_1_q[1]);
  not not_7 (not_7_out, counter_1_q[2]);
  ExactlyOne xor_1 (.out(xor_1_out), .in0(out_18[4]), .in1(xnor_2_out), .in2(out_14));
  ExactlyOne xor_2 (.out(xor_2_out), .in0(out_18[5]), .in1(xnor_2_out), .in2(out_15));
  ExactlyOne xor_3 (.out(xor_3_out), .in0(out_18[6]), .in1(xnor_2_out), .in2(out_16));
  ExactlyOne xor_4 (.out(xor_4_out), .in0(out_18[7]), .in1(xnor_2_out), .in2(out_17));
  Comparator comparator_1 (
    .Sub(and_5_out), .A0(out_18[4]), .B0(in_4), .A1(out_18[5]), .B1(in_3), .A2(out_18[6]), .B2(in_2),
    .A3(out_18[7]), .B3(in_1), .S0(out_14), .S1(out_15), .S2(out_16), .S3(out_17));  // open: Cout
  and and_6 (QRld, not_5_out, not_6_out, not_7_out);
  or or_7 (ashr, xor_1_out, xor_2_out, xor_3_out, xor_4_out);

  // Other names for the same wires on the sheet: AC0 = out_14; AC1 = out_15; AC2 = out_16; AC3 = out_17; B0 = in_4;
  //   B1 = in_3; B2 = in_2; B3 = in_1; q0_t = out_18[0]; Qn = out_18[0]; q1_t = out_18[1]; q2_t = out_18[2];
  //   q3_t = out_18[3]; A0_t = out_18[4]; A1_t = out_18[5]; A2_t = out_18[6]; A3_t = out_18[7]; Q0 = in_8; Q1 = in_7;
  //   Q2 = in_6; Q3 = in_5
endmodule

module Comparator (
  input  Sub,
  input  A0,
  input  B0,
  input  A1,
  input  B1,
  input  A2,
  input  B2,
  input  A3,
  input  B3,
  output S0,
  output S1,
  output S2,
  output S3,
  output Cout
);

  wire adder_1_cout, adder_2_cout, adder_3_cout, xor_1_out, xor_2_out, xor_3_out, xor_4_out;

  xor xor_1 (xor_1_out, Sub, B0);
  xor xor_2 (xor_2_out, Sub, B1);
  xor xor_3 (xor_3_out, Sub, B2);
  xor xor_4 (xor_4_out, Sub, B3);
  Adder #(.width(1)) adder_1 (.a(A0), .b(xor_1_out), .out(S0), .cin(Sub), .cout(adder_1_cout));
  Adder #(.width(1)) adder_2 (.a(A1), .b(xor_2_out), .out(S1), .cin(adder_1_cout), .cout(adder_2_cout));
  Adder #(.width(1)) adder_3 (.a(A2), .b(xor_3_out), .out(S2), .cin(adder_2_cout), .cout(adder_3_cout));
  Adder #(.width(1)) adder_4 (.a(A3), .b(xor_4_out), .out(S3), .cin(adder_3_cout), .cout(Cout));
endmodule
